# Fritzing sketch CircuitDiagram (saved by Fritzing 0.9.3b)
breadboards: 1

parts:
  Part3 = Arduino Leonardo (Rev3b)
  S5 = Momentary Switch [package=ksa_sealed_tac_switch]
  Part4 = Adafruit Analog 2-Axis Joystick [part_number="Adafruit #512"]
  S6 = Momentary Switch [package=ksa_sealed_tac_switch]
  S7 = Momentary Switch [package=ksa_sealed_tac_switch]

nets:
  N1: Part3.D2/SDA, Part4.SWITCH
  N2: Part3.D3_PWM/SCL, S6.3
  N3: Part3.D4/A6, S5.3
  N4: Part3.D5_PWM, S7.3
  GND: Part3.GND, S5.1, Part4.GND, S6.1, S7.1
  N5: Part3.A0, Part4.XOUT
  N6: Part3.A1, Part4.YOUT

custom parts:
  Adafruit Analog 2-Axis Joystick: This mini-kit makes it easy to mount a PSP/Xbox-like thumb joystick to your project. The thumbstick is an analog joystick - more accurate and sensitive than just 'directional' joysticks - with a 'press in to select' button. Since it's analog, you'll need two analog reading pins on your microcontroller to determine X and Y. Having an extra digital input will let you read the switch. The pack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
